# Fritzing sketch ClockModule (saved by Fritzing 0.9.3b)
stripboards: 2
perfboards: 1

parts:
  S1 = Pushbutton [package="[THT]"]
  S4 = Toggle Switch [package=THT]
  LED4 = LED - 5mm [color="Yellow (595nm)" package="5 mm [THT]"]
  IC2 = IC, DIP package, 14 pins [chip_label=74LS08]
  IC3 = IC, DIP package, 14 pins [chip_label=74LS32]
  U1 = 555 Timer [package="SO8 [SMD]"]
  U2 = 555 Timer [package="SO8 [SMD]"]  # not connected
  U3 = 555 Timer [package="SO8 [SMD]"]
  S5 = Toggle Switch [package=THT]
  R1 = Resistor [tolerance=±5% resistance=220 package="2512 [SMD]"]
  R7 = Resistor [tolerance=±5% resistance=220 package="2512 [SMD]"]
  R8 = Resistor [tolerance=±5% resistance=220 package="2512 [SMD]"]
  R10 = TRIMPOT [package=3386u]
  C4 = Ceramic Capacitor [capacitance="100 nF" package="0603 [SMD, multilayer]"]
  C5 = Ceramic Capacitor [capacitance=0.1µF package="0603 [SMD, multilayer]"]
  C6 = Electrolytic Capacitor [capacitance=100μF package="0807 [SMD, electrolytic]"]
  IC1 = IC, DIP package, 14 pins [chip_label=74LS04]
  LED5 = LED - 5mm [color="Yellow (595nm)" package="5 mm [THT]"]
  LED6 = LED - 5mm [color="Yellow (595nm)" package="5 mm [THT]"]
  LED7 = LED - 5mm [color="Blue (430nm)" package="5 mm [THT]"]
  R11 = Resistor [tolerance=±5% resistance=220 package="2512 [SMD]"]
  C7 = Ceramic Capacitor [capacitance="100 nF" package="0603 [SMD, multilayer]"]
  C8 = Ceramic Capacitor [capacitance="100 nF" package="0603 [SMD, multilayer]"]
  R12 = Resistor [tolerance=±5% resistance=220 package="2512 [SMD]"]
  R13 = Resistor [tolerance=±5% resistance=220 package="2512 [SMD]"]
  R14 = Resistor [tolerance=±5% resistance=220 package="2512 [SMD]"]
  R15 = Resistor [tolerance=±5% resistance=220 package="2512 [SMD]"]  # not connected
  R16 = Resistor [tolerance=±5% resistance=220 package="2512 [SMD]"]
  C9 = Ceramic Capacitor [capacitance="100 nF" package="0603 [SMD, multilayer]"]  # not connected
  C10 = Ceramic Capacitor [capacitance=0.1µF package="0603 [SMD, multilayer]"]
  J3 = double row female pin header, 20 pins [form="♀ (female)"]
  J5 = double row female pin header, 20 pins [form="♀ (female)"]
  J6 = double row female pin header, 20 pins [form="♀ (female)"]
  J7 = double row female pin header, 20 pins [form="♀ (female)"]

nets:
  N1: S1.Pin_1, S1.Pin_2
  N2: S1.Pin_3, S1.Pin_4, IC2.pin7, U1.Pin_1, U3.Pin_1, U3.Pin_2, R1.Pin_1, C4.1, R11.Pin_0, C7.1, C8.0, C10.0, J3.pin1
  N3: S4.L1, R16.Pin_0
  N4: LED4.cathode, U1.Pin_3
  N5: LED4.anode, R1.Pin_0
  N6: IC2.pin1, IC1.pin1
  N7: IC2.pin2, C6.+
  N8: IC2.pin3, IC3.pin1
  N9: IC2.pin4, IC1.pin2
  N10: IC2.pin6, IC3.pin2
  N11: IC2.pin8, LED7.cathode
  N12: IC2.pin9, IC3.pin3
  N13: IC2.pin10, IC1.pin8
  N14: IC3.pin14, U1.Pin_4, U1.Pin_8, U3.Pin_8, R8.Pin_0, R11.Pin_1, R12.Pin_0, R16.Pin_1, C10.1, J6.pin1
  N15: U1.Pin_6, R10.WIPER
  N16: S5.L1, IC1.pin9
  N17: R7.Pin_0, R8.Pin_1
  N18: C5.0, J5.pin20
  N19: C5.1, J7.pin20
  N20: LED5.anode, R13.Pin_0
  N21: LED6.anode, R14.Pin_0
  N22: R13.Pin_1, R14.Pin_1
