// Digital circuit FullAdder.dig as structural Verilog
module FullAdder (
  input  A,
  input  B,
  input  Ci,
  output S,
  output Co
);

  wire halfadder_1_co, halfadder_1_s, halfadder_2_co;

  HalfAdder halfadder_1 (.A(A), .B(B), .S(halfadder_1_s), .Co(halfadder_1_co));
  HalfAdder halfadder_2 (.A(halfadder_1_s), .B(Ci), .S(S), .Co(halfadder_2_co));
  or or_1 (Co, halfadder_1_co, halfadder_2_co);

  // Notes on the sheet:
  //   S: Sum
  //   Co: Carry out
  //   Ci: Carry In
endmodule

/* Test case:
A B Ci S Co
0 0 0  0 0
0 0 1  1 0
0 1 0  1 0
0 1 1  0 1
1 0 0  1 0
1 0 1  0 1
1 1 1  1 1
*/
