// Digital circuit HalfAdder.dig as structural Verilog
module HalfAdder (
  input  A,
  input  B,
  output S,
  output Co
);

  xor xor_1 (S, A, B);
  and and_1 (Co, A, B);

  // Notes on the sheet:
  //   S: Sum
  //   Co: Carry
endmodule

/* Test case:
A B S Co
0 0 0 0
0 1 1 0
1 0 1 0
1 1 0 1
*/
