// Logisim project HalfAdder.circ as structural Verilog: 1 circuit, main circuit main
module main (
  input  A,
  input  B,
  output Sum,
  output Carry_Out
);

  xor xor_1 (Sum, A, B);
  and and_1 (Carry_Out, A, B);
endmodule
